# Fritzing sketch blink_led (saved by Fritzing 0.7.10b)
breadboards: 1

parts:
  LED2 = LED - 5mm [color="Red (633nm)" package="5 mm [THT]"]
  Arduino1 = Arduino

nets:
  N1: LED2.cathode, Arduino1.GND
  N2: LED2.anode, Arduino1.D13
